# Fritzing sketch chicken-run (saved by Fritzing 0.9.3b)
breadboards: 1

parts:
  Raspberry_Pi1 = Raspberry Pi (Model B)
  R1 = Resistor [tolerance=±5% resistance=220 package=THT]
  LED1 = LED - 5mm [color="White (6500K)" package="5 mm [THT]"]
  Q1 = PNP-Transistor [package="TO92 [THT]"]
  R2 = Resistor [tolerance=±5% resistance=680k package=THT]

nets:
  N1: Raspberry_Pi1.5V, R1.Pin_1
  N2: Raspberry_Pi1.SCL, R2.Pin_1
  N3: Raspberry_Pi1.GND, Q1.C
  N4: R1.Pin_0, LED1.anode
  N5: LED1.cathode, Q1.E
  N6: Q1.B, R2.Pin_0

custom parts:
  Raspberry Pi (Model B): Raspberry Pi Single-board Computer, Model B
